// Logisim project Exercise3.circ as structural Verilog: 1 circuit, main circuit main
module main (
  input  in_1
);

  wire _1_out, _2_out, _3_out, _4_out, _5_out, _6_out, clock_1_out, d_ff_1_q, d_ff_1_qn, d_ff_2_q, d_ff_2_qn;

  Clock clock_1 (.out(clock_1_out));
  nand _1 (_1_out, in_1, in_1);
  nand _2 (_2_out, d_ff_1_q, _1_out);
  nand _3 (_3_out, in_1, d_ff_1_qn);
  nand _4 (_4_out, d_ff_1_qn, _1_out);
  nand _6 (_6_out, _2_out, _3_out);
  nand _5 (_5_out, _4_out, _4_out);
  D_Flip_Flop d_ff_1 (.clk(clock_1_out), .D(_6_out), .Q(d_ff_1_q), .Qn(d_ff_1_qn));  // open: preset, en, reset
  D_Flip_Flop d_ff_2 (.clk(clock_1_out), .D(_5_out), .Q(d_ff_2_q), .Qn(d_ff_2_qn));  // open: preset, en, reset
  LED led_1 (.in(d_ff_1_q));
  LED led_2 (.in(d_ff_1_qn));
  LED led_3 (.in(d_ff_2_q));
  LED led_4 (.in(d_ff_2_qn));

  // Notes on the sheet:
  //   1-flip
  //   2- flip
endmodule
